// Logisim project alu.circ as structural Verilog: 14 circuits, main circuit main
module main (
  input  [15:0] X,
  input  [15:0] Y,
  input  [3:0] switch__S,
  output signed_overflow,
  output [15:0] result,
  output equal
);

  wire add_1_signed_overflow, comparator_1_eq, comparator_2_eq, or_1_out, or_3_out, sub_1_signed_overflow;
  wire [15:0] add_1_sum, and_1_out, bc_1_out, ffo_1_out, or_2_out, sllv_1_out, slt_1_out, srav_1_out,
       srlv_1_out, sub_1_sum, zb_1_out;

  Comparator #(.width(4)) comparator_1 (.a(switch__S), .b(4'b0110), .eq(comparator_1_eq));  // open: gt, lt
  Comparator #(.width(4)) comparator_2 (.a(switch__S), .b(4'b0111), .eq(comparator_2_eq));  // open: gt, lt
  or or_1 (or_1_out, comparator_1_eq, comparator_2_eq);
  AND and_1 (.in_1(X), .in_2(Y), .out(and_1_out));
  OR or_2 (.in_1(X), .in_2(Y), .out(or_2_out));
  SLT slt_1 (.in_1(X), .in_2(Y), .out(slt_1_out));
  SLLV sllv_1 (.in_1(X), .in_2(Y), .out(sllv_1_out));
  SRLV srlv_1 (.in_1(X), .in_2(Y), .out(srlv_1_out));
  SRAV srav_1 (.in_1(X), .in_2(Y), .out(srav_1_out));
  ADD add_1 (.X(X), .Y(Y), .SUM(add_1_sum), .signed_overflow(add_1_signed_overflow));
  SUB sub_1 (.X(X), .Y(Y), .SUM(sub_1_sum), .signed_overflow(sub_1_signed_overflow));
  Comparator #(.width(16)) comparator_3 (.a(X), .b(Y), .eq(equal));  // open: gt, lt
  ffo ffo_1 (.rs(X), .out(ffo_1_out));
  zb zb_1 (.rs(X), .out(zb_1_out));
  bc bc_1 (.rs(X), .out(bc_1_out));
  or or_3 (or_3_out, sub_1_signed_overflow, add_1_signed_overflow);
  and and_2 (signed_overflow, or_3_out, or_1_out);
  Multiplexer #(.select(4), .width(16)) multiplexer_1 (
    .in0(and_1_out), .in1(or_2_out), .in2(slt_1_out), .in3(sllv_1_out), .in4(srlv_1_out), .in5(srav_1_out),
    .in6(add_1_sum), .in7(sub_1_sum), .in8(ffo_1_out), .in9(zb_1_out), .in10(bc_1_out), .in11({16{1'b0}}),
    .in12({16{1'b0}}), .in13({16{1'b0}}), .in14({16{1'b0}}), .in15({16{1'b0}}), .out(result), .sel(switch__S));  // open: en

  // Notes on the sheet:
  //   These are INPUTS to your circuit
  //   This is an INPUT to your circuit
  //   DO NOT CHANGE THE LOCATIONS OF THE INPUTS/OUTPUTS! IF YOU DO SO, YOU NEED TO MAKE SURE THE PINS ARE AT THE RIGHT PLACE!
  //   These are OUTPUTS to your circuit
endmodule

module AND (
  input  [15:0] in_1,
  input  [15:0] in_2,
  output [15:0] out
);

  assign out = in_1 & in_2;  // AND_Gate and_1, 16 bits wide
endmodule

module OR (
  input  [15:0] in_1,
  input  [15:0] in_2,
  output [15:0] out
);

  assign out = in_1 | in_2;  // OR_Gate or_1, 16 bits wide
endmodule

module SLT (
  input  [15:0] in_1,
  input  [15:0] in_2,
  output [15:0] out
);

  wire comparator_1_lt;

  Comparator #(.width(16)) comparator_1 (.a(in_1), .b(in_2), .lt(comparator_1_lt));  // open: gt, eq
  assign out = {{15{1'b0}}, comparator_1_lt};  // Bit_Extender bit_extender_1
endmodule

module SLLV (
  input  [15:0] in_1,
  input  [15:0] in_2,
  output [15:0] out
);

  Shifter #(.width(16)) shifter_1 (.in(in_1), .\dist (in_2[3:0]), .out(out));

  assign in_2[11:4] = {in_2[15:12], in_2[15:12]};
  // also tied to GND on the sheet: {in_2[12], in_2[13], in_2[14], in_2[15]}
endmodule

module SRLV (
  input  [15:0] in_1,
  input  [15:0] in_2,
  output [15:0] out
);

  Shifter #(.width(16), .shift("lr")) shifter_1 (.in(in_1), .\dist (in_2[3:0]), .out(out));

  assign in_2[11:4] = {in_2[15:12], in_2[15:12]};
  // also tied to GND on the sheet: {in_2[12], in_2[13], in_2[14], in_2[15]}
endmodule

module SRAV (
  input  [15:0] in_1,
  input  [15:0] in_2,
  output [15:0] out
);

  Shifter #(.width(16), .shift("ar")) shifter_1 (.in(in_1), .\dist (in_2[3:0]), .out(out));

  assign in_2[11:4] = {in_2[15:12], in_2[15:12]};
  // also tied to GND on the sheet: {in_2[12], in_2[13], in_2[14], in_2[15]}
endmodule

module ADD (
  input  [15:0] X,
  input  [15:0] Y,
  output [15:0] SUM,
  output signed_overflow
);

  wire add_8bit_1_carryout, add_8bit_2_carryout;

  check_overflow check_overflow_1 (.X(X), .Y(Y), .SUM(SUM), .signed_overflow(signed_overflow));
  add_8bit add_8bit_1 (
    .x(X[15:8]), .y(Y[15:8]), .carry_in(add_8bit_2_carryout), .sum(SUM[15:8]), .carryout(add_8bit_1_carryout));
  add_8bit add_8bit_2 (.x(X[7:0]), .y(Y[7:0]), .carry_in(1'b0), .sum(SUM[7:0]), .carryout(add_8bit_2_carryout));
  // also tied to GND on the sheet: add_8bit_1_carryout
endmodule

module SUB (
  input  [15:0] X,
  input  [15:0] Y,
  output [15:0] SUM,
  output signed_overflow
);

  wire add_8bit_1_carryout, add_8bit_2_carryout;
  wire [15:0] adder_1_out, not_1_out;

  assign not_1_out = ~Y;  // NOT_Gate not_1, 16 bits wide
  check_overflow check_overflow_1 (.X(X), .Y(adder_1_out), .SUM(SUM), .signed_overflow(signed_overflow));
  Adder #(.width(16)) adder_1 (.a(not_1_out), .b(16'h1), .out(adder_1_out));  // open: cin, cout
  add_8bit add_8bit_1 (
    .x(X[7:0]), .y(adder_1_out[7:0]), .sum(SUM[7:0]), .carryout(add_8bit_1_carryout));  // open: carry_in
  add_8bit add_8bit_2 (
    .x(X[15:8]), .y(adder_1_out[15:8]), .carry_in(add_8bit_1_carryout), .sum(SUM[15:8]),
    .carryout(add_8bit_2_carryout));
  // also tied to GND on the sheet: add_8bit_2_carryout
endmodule

module add_8bit (
  input  [7:0] x,
  input  [7:0] y,
  input  carry_in,
  output [7:0] sum,
  output carryout
);

  wire adder_1_cout, adder_2_cout, adder_3_cout, adder_4_cout, adder_5_cout, adder_6_cout, adder_7_cout;

  Adder #(.width(1)) adder_1 (.a(x[0]), .b(y[0]), .out(sum[0]), .cin(carry_in), .cout(adder_1_cout));
  Adder #(.width(1)) adder_2 (.a(x[1]), .b(y[1]), .out(sum[1]), .cin(adder_1_cout), .cout(adder_2_cout));
  Adder #(.width(1)) adder_3 (.a(x[2]), .b(y[2]), .out(sum[2]), .cin(adder_2_cout), .cout(adder_3_cout));
  Adder #(.width(1)) adder_4 (.a(x[3]), .b(y[3]), .out(sum[3]), .cin(adder_3_cout), .cout(adder_4_cout));
  Adder #(.width(1)) adder_5 (.a(x[4]), .b(y[4]), .out(sum[4]), .cin(adder_4_cout), .cout(adder_5_cout));
  Adder #(.width(1)) adder_6 (.a(x[5]), .b(y[5]), .out(sum[5]), .cin(adder_5_cout), .cout(adder_6_cout));
  Adder #(.width(1)) adder_7 (.a(x[6]), .b(y[6]), .out(sum[6]), .cin(adder_6_cout), .cout(adder_7_cout));
  Adder #(.width(1)) adder_8 (.a(x[7]), .b(y[7]), .out(sum[7]), .cin(adder_7_cout), .cout(carryout));
endmodule

module check_overflow (
  input  [15:0] X,
  input  [15:0] Y,
  input  [15:0] SUM,
  output signed_overflow
);

  wire and_1_out, and_2_out, not_1_out, not_2_out, not_3_out;

  not not_1 (not_1_out, Y[15]);
  not not_2 (not_2_out, X[15]);
  and and_1 (and_1_out, not_2_out, not_1_out, SUM[15]);
  or or_1 (signed_overflow, and_1_out, and_2_out);
  not not_3 (not_3_out, SUM[15]);
  and and_2 (and_2_out, X[15], Y[15], not_3_out);

  assign X[14:0] = SUM[14:0];
  assign Y[14:0] = SUM[14:0];
  // also tied to GND on the sheet: {SUM[0], SUM[1], SUM[2], SUM[3], SUM[4], SUM[5], SUM[6], SUM[7], SUM[8], SUM[9], SUM[10], SUM[11], SUM[12], SUM[13], SUM[14]}
endmodule

module ffo (
  input  [15:0] rs,
  output [15:0] out
);

  wire comparator_1_eq;
  wire [3:0] bitfinder_1_index, subtractor_1_out;
  wire [15:0] bit_extender_1_out;

  BitFinder #(.width(16), .\type ("high1")) bitfinder_1 (.in(rs), .index(bitfinder_1_index));  // open: found
  Subtractor #(.width(4)) subtractor_1 (.a(4'b1111), .b(bitfinder_1_index), .out(subtractor_1_out));  // open: bin, bout
  assign bit_extender_1_out = {{12{1'b0}}, subtractor_1_out};  // Bit_Extender bit_extender_1
  Comparator #(.width(16)) comparator_1 (.a(rs), .b({16{1'b0}}), .eq(comparator_1_eq));  // open: gt, lt
  Multiplexer #(.width(16)) multiplexer_1 (
    .in0(bit_extender_1_out), .in1(16'h10), .out(out), .sel(comparator_1_eq));  // open: en
endmodule

module zb (
  input  [15:0] rs,
  output [15:0] out
);

  wire comparator_1_eq, comparator_2_eq, or_1_out;

  Comparator comparator_1 (.a(rs[7:0]), .b({8{1'b0}}), .eq(comparator_1_eq));  // open: gt, lt
  Comparator comparator_2 (.a({8{1'b0}}), .b(rs[15:8]), .eq(comparator_2_eq));  // open: gt, lt
  or or_1 (or_1_out, comparator_1_eq, comparator_2_eq);
  assign out = {{15{1'b0}}, or_1_out};  // Bit_Extender bit_extender_1
endmodule

module bc (
  input  [15:0] rs,
  output [15:0] out
);

  wire adder_16_cout;
  wire [3:0] adder_1_out, adder_2_out, adder_3_out, adder_4_out, adder_5_out, adder_6_out, adder_7_out,
       adder_8_out, adder_9_out, adder_10_out, adder_11_out, adder_12_out, adder_13_out, adder_14_out,
       adder_15_out, adder_16_out, bit_extender_1_out, bit_extender_2_out, bit_extender_3_out,
       bit_extender_4_out, bit_extender_5_out, bit_extender_6_out, bit_extender_7_out, bit_extender_8_out,
       bit_extender_9_out, bit_extender_10_out, bit_extender_11_out, bit_extender_12_out,
       bit_extender_13_out, bit_extender_14_out, bit_extender_15_out, bit_extender_16_out;
  wire [15:0] bit_extender_17_out;

  assign bit_extender_1_out = {{3{1'b0}}, rs[0]};  // Bit_Extender bit_extender_1
  assign bit_extender_2_out = {{3{1'b0}}, rs[1]};  // Bit_Extender bit_extender_2
  assign bit_extender_3_out = {{3{1'b0}}, rs[2]};  // Bit_Extender bit_extender_3
  assign bit_extender_4_out = {{3{1'b0}}, rs[3]};  // Bit_Extender bit_extender_4
  assign bit_extender_5_out = {{3{1'b0}}, rs[4]};  // Bit_Extender bit_extender_5
  assign bit_extender_6_out = {{3{1'b0}}, rs[5]};  // Bit_Extender bit_extender_6
  assign bit_extender_7_out = {{3{1'b0}}, rs[6]};  // Bit_Extender bit_extender_7
  assign bit_extender_8_out = {{3{1'b0}}, rs[7]};  // Bit_Extender bit_extender_8
  assign bit_extender_9_out = {{3{1'b0}}, rs[8]};  // Bit_Extender bit_extender_9
  assign bit_extender_10_out = {{3{1'b0}}, rs[9]};  // Bit_Extender bit_extender_10
  assign bit_extender_11_out = {{3{1'b0}}, rs[10]};  // Bit_Extender bit_extender_11
  assign bit_extender_12_out = {{3{1'b0}}, rs[11]};  // Bit_Extender bit_extender_12
  assign bit_extender_13_out = {{3{1'b0}}, rs[12]};  // Bit_Extender bit_extender_13
  assign bit_extender_14_out = {{3{1'b0}}, rs[13]};  // Bit_Extender bit_extender_14
  assign bit_extender_15_out = {{3{1'b0}}, rs[14]};  // Bit_Extender bit_extender_15
  assign bit_extender_16_out = {{3{1'b0}}, rs[15]};  // Bit_Extender bit_extender_16
  Adder #(.width(4)) adder_1 (.a(bit_extender_1_out), .b(4'b0000), .out(adder_1_out));  // open: cin, cout
  Adder #(.width(4)) adder_2 (.a(adder_1_out), .b(bit_extender_2_out), .out(adder_2_out));  // open: cin, cout
  Adder #(.width(4)) adder_3 (.a(adder_2_out), .b(bit_extender_3_out), .out(adder_3_out));  // open: cin, cout
  Adder #(.width(4)) adder_4 (.a(adder_3_out), .b(bit_extender_4_out), .out(adder_4_out));  // open: cin, cout
  Adder #(.width(4)) adder_5 (.a(adder_4_out), .b(bit_extender_5_out), .out(adder_5_out));  // open: cin, cout
  Adder #(.width(4)) adder_6 (.a(adder_5_out), .b(bit_extender_6_out), .out(adder_6_out));  // open: cin, cout
  Adder #(.width(4)) adder_7 (.a(adder_6_out), .b(bit_extender_7_out), .out(adder_7_out));  // open: cin, cout
  Adder #(.width(4)) adder_8 (.a(adder_7_out), .b(bit_extender_8_out), .out(adder_8_out));  // open: cin, cout
  Adder #(.width(4)) adder_9 (.a(adder_8_out), .b(bit_extender_9_out), .out(adder_9_out));  // open: cin, cout
  Adder #(.width(4)) adder_10 (.a(adder_9_out), .b(bit_extender_10_out), .out(adder_10_out));  // open: cin, cout
  Adder #(.width(4)) adder_11 (.a(adder_10_out), .b(bit_extender_11_out), .out(adder_11_out));  // open: cin, cout
  Adder #(.width(4)) adder_12 (.a(adder_11_out), .b(bit_extender_12_out), .out(adder_12_out));  // open: cin, cout
  Adder #(.width(4)) adder_13 (.a(adder_12_out), .b(bit_extender_13_out), .out(adder_13_out));  // open: cin, cout
  Adder #(.width(4)) adder_14 (.a(adder_13_out), .b(bit_extender_14_out), .out(adder_14_out));  // open: cin, cout
  Adder #(.width(4)) adder_15 (.a(adder_14_out), .b(bit_extender_15_out), .out(adder_15_out));  // open: cin, cout
  assign bit_extender_17_out = {{12{1'b0}}, adder_16_out};  // Bit_Extender bit_extender_17
  Adder #(.width(4)) adder_16 (
    .a(adder_15_out), .b(bit_extender_16_out), .out(adder_16_out), .cout(adder_16_cout));  // open: cin
  Multiplexer #(.width(16)) multiplexer_1 (
    .in0(bit_extender_17_out), .in1(16'h10), .out(out), .sel(adder_16_cout));  // open: en
endmodule
