// Logisim project cpu.circ as structural Verilog: 4 circuits, main circuit main
module main (
  input  [15:0] From_Instr_Mem,
  input  clk,
  output [15:0] r0,
  output [15:0] r1,
  output [15:0] r2,
  output [15:0] r3,
  output [15:0] Display_0,
  output [15:0] Display_1,
  output [15:0] To_Instr_Mem,
  output [15:0] Data_Mem_Data,
  output [15:0] Data_Mem_Addr,
  output Data_Mem_Write
);

  wire ALUsrc, and_2_out, and_3_out, BNE, Branch, BranchTaken, button_1_out, disp, jal, jr, jump, lui,
       main_2_equal, MRd, MtoR, not_1_out, not_2_out, or_1_out, RegDst, RWrite, \signed , so;
  wire [1:0] multiplexer_3_out, multiplexer_4_out;
  wire [2:0] ALUop;
  wire [3:0] alucontrol_1_out_3;
  wire [15:0] adder_1_out, adder_2_out, and_1_out, bit_extender_1_out, bit_extender_2_out,
       bit_extender_3_out, imm, main_1_read_data_2, multiplexer_1_out, multiplexer_8_out, multiplexer_9_out,
       multiplexer_10_out, multiplexer_11_out, multiplexer_12_out, multiplexer_13_out, or_2_out,
       register_1_q, rs, Rt_Imm, X, Y;

  Register #(.width(16)) PC (.D(multiplexer_12_out), .Q(To_Instr_Mem), .clk(clk));  // open: en, clr
  or or_1 (or_1_out, jump, jal, jr, BranchTaken);
  Multiplexer #(.width(16)) multiplexer_1 (
    .in0(From_Instr_Mem), .in1({16{1'b0}}), .out(multiplexer_1_out), .sel(or_1_out));  // open: en
  Register #(.width(16)) register_1 (.D(multiplexer_1_out), .Q(register_1_q), .clk(clk));  // open: en, clr
  Control control_1 (
    ._15_12(register_1_q[15:12]), .RegDst(RegDst), .Branch(Branch), .BNE(BNE), .ALUop(ALUop),
    .ALUsrc(ALUsrc), .RegWrite(RWrite), .MemtoReg(MtoR), .MemRead(MRd), .MemWrite(Data_Mem_Write),
    .\signed (\signed ), .jump(jump), .jal(jal), .jr(jr), .lui(lui), .disp(disp));
  assign bit_extender_1_out = {{8{1'b0}}, register_1_q[7:0]};  // Bit_Extender bit_extender_1
  assign bit_extender_2_out = {{8{register_1_q[7]}}, register_1_q[7:0]};  // Bit_Extender bit_extender_2
  assign bit_extender_3_out = {{4{1'b0}}, register_1_q[11:0]};  // Bit_Extender bit_extender_3
  Multiplexer #(.width(16)) multiplexer_2 (
    .in0(bit_extender_1_out), .in1(bit_extender_2_out), .out(imm), .sel(\signed ));  // open: en
  ALUcontrol alucontrol_1 (._5_0(register_1_q[5:0]), .ALUop(ALUop), .out_3(alucontrol_1_out_3));
  Multiplexer #(.width(2)) multiplexer_3 (
    .in0(register_1_q[9:8]), .in1(register_1_q[7:6]), .out(multiplexer_3_out), .sel(RegDst));  // open: en
  assign and_1_out = 16'hf000 & To_Instr_Mem;  // AND_Gate and_1, 16 bits wide
  Multiplexer #(.width(2)) multiplexer_4 (
    .in0(multiplexer_3_out), .in1(2'b11), .out(multiplexer_4_out), .sel(jal));  // open: en
  assign or_2_out = and_1_out | bit_extender_3_out;  // OR_Gate or_2, 16 bits wide
  Regfile_main main_1 (
    .Read_register_1(register_1_q[11:10]), .Read_register_2(register_1_q[9:8]),
    .write_register(multiplexer_4_out), .write_data(multiplexer_13_out), .Reg_0_Value(r0), .Reg_1_Value(r1),
    .Reg_2_Value(r2), .Reg_3_Value(r3), .RegWrite(RWrite), .clock(clk), .Read_Data_1(rs),
    .Read_Data_2(main_1_read_data_2));
  Multiplexer #(.width(16)) multiplexer_5 (.in0(rs), .in1(imm), .out(X), .sel(lui));  // open: en
  Multiplexer #(.width(16)) multiplexer_6 (.in0(Rt_Imm), .in1(16'h8), .out(Y), .sel(lui));  // open: en
  Display u_display_1 (.sel(imm[0]), .ctrl(disp), .Input_0(rs), .clk(clk), .Output_0(Display_0), .Output_1(Display_1));
  Adder #(.width(16)) adder_1 (.a(To_Instr_Mem), .b(16'h1), .out(adder_1_out));  // open: cin, cout
  alu_main main_2 (
    .switch__S(alucontrol_1_out_3), .X(X), .equal(main_2_equal), .result(Data_Mem_Addr),
    .signed_overflow(so), .Y(Y));
  Multiplexer #(.width(16)) multiplexer_7 (
    .in0(main_1_read_data_2), .in1(imm), .out(Rt_Imm), .sel(ALUsrc));  // open: en
  Multiplexer #(.width(16)) multiplexer_8 (
    .in0(adder_1_out), .in1(To_Instr_Mem), .out(multiplexer_8_out), .sel(BranchTaken));  // open: en
  not not_1 (not_1_out, main_2_equal);
  Hex_Digit_Display hex_digit_display_1 (.value(Display_0[3:0]));  // open: dp
  Hex_Digit_Display hex_digit_display_2 (.value(Display_0[7:4]));  // open: dp
  and and_2 (and_2_out, Branch, main_2_equal);
  or or_3 (BranchTaken, and_2_out, and_3_out);
  and and_3 (and_3_out, BNE, not_1_out);
  not not_2 (not_2_out, Data_Mem_Write);
  Button button_1 (.out(button_1_out));
  Hex_Digit_Display hex_digit_display_3 (.value(Display_0[11:8]));  // open: dp
  Hex_Digit_Display hex_digit_display_4 (.value(Display_0[15:12]));  // open: dp
  Multiplexer #(.width(16)) multiplexer_9 (
    .in0(multiplexer_8_out), .in1(adder_2_out), .out(multiplexer_9_out), .sel(BranchTaken));  // open: en
  Adder #(.width(16)) adder_2 (.a(multiplexer_8_out), .b(imm), .out(adder_2_out));  // open: cin, cout
  assign Data_Mem_Data = Data_Mem_Write ? main_1_read_data_2 : 16'bz;  // Controlled_Buffer controlled_buffer_1
  RAM #(.addrWidth(16), .dataWidth(16)) ram_1 (
    .addr(Data_Mem_Addr), .data(Data_Mem_Data), .sel(1'b1), .clk(clk), .ld(not_2_out), .clr(button_1_out));
  Hex_Digit_Display hex_digit_display_5 (.value(Display_1[3:0]));  // open: dp
  Multiplexer #(.width(16)) multiplexer_10 (
    .in0(multiplexer_9_out), .in1(or_2_out), .out(multiplexer_10_out), .sel(jump));  // open: en
  Multiplexer #(.width(16)) multiplexer_11 (
    .in0(Data_Mem_Addr), .in1(Data_Mem_Data), .out(multiplexer_11_out), .sel(MtoR));  // open: en
  Hex_Digit_Display hex_digit_display_6 (.value(Display_1[11:8]));  // open: dp
  Hex_Digit_Display hex_digit_display_7 (.value(Display_1[7:4]));  // open: dp
  Multiplexer #(.width(16)) multiplexer_12 (
    .in0(multiplexer_10_out), .in1(rs), .out(multiplexer_12_out), .sel(jr));  // open: en
  Multiplexer #(.width(16)) multiplexer_13 (
    .in0(multiplexer_11_out), .in1(To_Instr_Mem), .out(multiplexer_13_out), .sel(jal));  // open: en
  Hex_Digit_Display hex_digit_display_8 (.value(Display_1[15:12]));  // open: dp
  LED led_1 (.in(so));

  // Other names for the same wires on the sheet: C = clk; d0[15:0] = Display_0; d1[15:0] = Display_1;
  //   MWrite = Data_Mem_Write; pcjal[15:0] = To_Instr_Mem

  // Notes on the sheet:
  //   This is the current PC that you need to send as OUTPUT
  //   This is the instruction that you would receive as INPUT
  //   Remember, this circuit is loaded from the harness to be tested!
  //   This is a CLK that is an INPUT driven from the harness.
  //   DO NOT CHANGE THE LOCATIONS OF THE INPUTS/OUTPUTS! IF YOU DO SO, YOU NEED TO MAKE SURE THE PINS ARE AT THE RIGHT PLACE!
  //   These are OUTPUTS to the circuit
  //   input X to ALU
  //   input Y to ALU
  //   Display 0
  //   Display 1
  //   These are OUTPUTS to the circuit
  //   Overflow
endmodule

module ALUcontrol (
  input  [5:0] _5_0,
  input  [2:0] ALUop,
  output [3:0] out_3
);

  wire decoder_1_out0, decoder_1_out1, decoder_1_out2, decoder_1_out3, decoder_1_out4, decoder_1_out5,
       decoder_1_out6, decoder_1_out7, not_1_out;
  wire [3:0] bitselector_1_out;

  Decoder #(.select(3), .enable("false")) decoder_1 (
    .out0(decoder_1_out0), .out1(decoder_1_out1), .out2(decoder_1_out2), .out3(decoder_1_out3),
    .out4(decoder_1_out4), .out5(decoder_1_out5), .out6(decoder_1_out6), .out7(decoder_1_out7), .sel(ALUop));
  BitSelector #(.width(6), .group(4)) bitselector_1 (.in(_5_0), .out(bitselector_1_out), .sel(not_1_out));
  not not_1 (not_1_out, decoder_1_out0);
  assign out_3 = decoder_1_out0 ? bitselector_1_out : 4'bz;  // Controlled_Buffer controlled_buffer_1
  assign out_3 = decoder_1_out1 ? 4'b0110 : 4'bz;  // Controlled_Buffer controlled_buffer_2
  assign out_3 = decoder_1_out3 ? 4'b0001 : 4'bz;  // Controlled_Buffer controlled_buffer_3
  assign out_3 = decoder_1_out2 ? 4'b0000 : 4'bz;  // Controlled_Buffer controlled_buffer_4
  assign out_3 = decoder_1_out5 ? 4'b1000 : 4'bz;  // Controlled_Buffer controlled_buffer_5
  assign out_3 = decoder_1_out4 ? 4'b0011 : 4'bz;  // Controlled_Buffer controlled_buffer_6
  assign out_3 = decoder_1_out6 ? 4'b1001 : 4'bz;  // Controlled_Buffer controlled_buffer_7
  assign out_3 = decoder_1_out7 ? 4'b1010 : 4'bz;  // Controlled_Buffer controlled_buffer_8
endmodule

module Control (
  input  [3:0] _15_12,
  output RegDst,
  output Branch,
  output BNE,
  output [2:0] ALUop,
  output ALUsrc,
  output RegWrite,
  output MemtoReg,
  output MemRead,
  output MemWrite,
  output \signed ,
  output jump,
  output jal,
  output jr,
  output lui,
  output disp
);

  wire decoder_1_out1, decoder_1_out2, decoder_1_out3, decoder_1_out4, decoder_1_out5, decoder_1_out6,
       decoder_1_out8;

  // Probe on _15_12
  Decoder #(.select(4), .enable("false")) decoder_1 (
    .out0(RegDst), .out1(decoder_1_out1), .out2(decoder_1_out2), .out3(decoder_1_out3),
    .out4(decoder_1_out4), .out5(decoder_1_out5), .out6(decoder_1_out6), .out7(jal), .out8(decoder_1_out8),
    .out9(jr), .out10(Branch), .out11(BNE), .out12(MemWrite), .out13(lui), .out14(MemRead), .out15(disp),
    .sel(_15_12));
  or or_1 (ALUsrc, decoder_1_out1, decoder_1_out2, decoder_1_out3, decoder_1_out4, decoder_1_out5, decoder_1_out6, MemWrite, lui, MemRead, disp);
  or or_2 (RegWrite, decoder_1_out3, RegDst, decoder_1_out1, decoder_1_out2, decoder_1_out4, jal, decoder_1_out5, decoder_1_out6, lui, MemRead);
  or or_3 (\signed , Branch, MemWrite, BNE, MemRead, decoder_1_out4);
  or or_4 (jump, decoder_1_out8, jal);
  Multiplexer #(.select(4), .width(3)) multiplexer_1 (
    .in0(3'b000), .in1(3'b101), .in2(3'b110), .in3(3'b111), .in4(3'b001), .in5(3'b010), .in6(3'b011),
    .in7(3'b111), .in8(3'b111), .in9(3'b111), .in10(3'b111), .in11(3'b111), .in12(3'b001), .in13(3'b100),
    .in14(3'b001), .in15(3'b111), .out(ALUop), .sel(_15_12));  // open: en
  or or_5 (MemtoReg, MemWrite, MemRead);
endmodule

module Display (
  input  sel,
  input  ctrl,
  input  [15:0] Input_0,
  input  clk,
  output [15:0] Output_0,
  output [15:0] Output_1
);

  wire and_1_out, and_2_out;

  and and_1 (and_1_out, ~sel, ctrl);  // AND_Gate
  and and_2 (and_2_out, sel, ctrl);
  Register #(.width(16)) register_1 (.D(Input_0), .en(and_1_out), .Q(Output_0), .clk(clk));  // open: clr
  Register #(.width(16)) register_2 (.D(Input_0), .en(and_2_out), .Q(Output_1), .clk(clk));  // open: clr
endmodule
